// Digital circuit 18bit RAM.dig as structural Verilog
module _18bit_RAM (
  input  RS1,
  input  RS2,
  input  W_EN,
  input  CLK,
  input  [17:0] WD_17_0,
  output [17:0] RD1_17_0,
  output [17:0] RD2_17_0
);

  _1bit_RAM _1bit_ram_1 (
    .WD(WD_17_0[0]), .RS1(RS1), .RS2(RS2), .sel(W_EN), .clk(CLK), .RD1(RD1_17_0[0]), .RD2(RD2_17_0[0]));
  _1bit_RAM _1bit_ram_2 (
    .WD(WD_17_0[1]), .RS1(RS1), .RS2(RS2), .sel(W_EN), .clk(CLK), .RD1(RD1_17_0[1]), .RD2(RD2_17_0[1]));
  _1bit_RAM _1bit_ram_3 (
    .WD(WD_17_0[2]), .RS1(RS1), .RS2(RS2), .sel(W_EN), .clk(CLK), .RD1(RD1_17_0[2]), .RD2(RD2_17_0[2]));
  _1bit_RAM _1bit_ram_4 (
    .WD(WD_17_0[3]), .RS1(RS1), .RS2(RS2), .sel(W_EN), .clk(CLK), .RD1(RD1_17_0[3]), .RD2(RD2_17_0[3]));
  _1bit_RAM _1bit_ram_5 (
    .WD(WD_17_0[4]), .RS1(RS1), .RS2(RS2), .sel(W_EN), .clk(CLK), .RD1(RD1_17_0[4]), .RD2(RD2_17_0[4]));
  _1bit_RAM _1bit_ram_6 (
    .WD(WD_17_0[5]), .RS1(RS1), .RS2(RS2), .sel(W_EN), .clk(CLK), .RD1(RD1_17_0[5]), .RD2(RD2_17_0[5]));
  _1bit_RAM _1bit_ram_7 (
    .WD(WD_17_0[6]), .RS1(RS1), .RS2(RS2), .sel(W_EN), .clk(CLK), .RD1(RD1_17_0[6]), .RD2(RD2_17_0[6]));
  _1bit_RAM _1bit_ram_8 (
    .WD(WD_17_0[7]), .RS1(RS1), .RS2(RS2), .sel(W_EN), .clk(CLK), .RD1(RD1_17_0[7]), .RD2(RD2_17_0[7]));
  _1bit_RAM _1bit_ram_9 (
    .WD(WD_17_0[8]), .RS1(RS1), .RS2(RS2), .sel(W_EN), .clk(CLK), .RD1(RD1_17_0[8]), .RD2(RD2_17_0[8]));
  _1bit_RAM _1bit_ram_10 (
    .WD(WD_17_0[9]), .RS1(RS1), .RS2(RS2), .sel(W_EN), .clk(CLK), .RD1(RD1_17_0[9]), .RD2(RD2_17_0[9]));
  _1bit_RAM _1bit_ram_11 (
    .WD(WD_17_0[10]), .RS1(RS1), .RS2(RS2), .sel(W_EN), .clk(CLK), .RD1(RD1_17_0[10]), .RD2(RD2_17_0[10]));
  _1bit_RAM _1bit_ram_12 (
    .WD(WD_17_0[11]), .RS1(RS1), .RS2(RS2), .sel(W_EN), .clk(CLK), .RD1(RD1_17_0[11]), .RD2(RD2_17_0[11]));
  _1bit_RAM _1bit_ram_13 (
    .WD(WD_17_0[12]), .RS1(RS1), .RS2(RS2), .sel(W_EN), .clk(CLK), .RD1(RD1_17_0[12]), .RD2(RD2_17_0[12]));
  _1bit_RAM _1bit_ram_14 (
    .WD(WD_17_0[13]), .RS1(RS1), .RS2(RS2), .sel(W_EN), .clk(CLK), .RD1(RD1_17_0[13]), .RD2(RD2_17_0[13]));
  _1bit_RAM _1bit_ram_15 (
    .WD(WD_17_0[14]), .RS1(RS1), .RS2(RS2), .sel(W_EN), .clk(CLK), .RD1(RD1_17_0[14]), .RD2(RD2_17_0[14]));
  _1bit_RAM _1bit_ram_16 (
    .WD(WD_17_0[15]), .RS1(RS1), .RS2(RS2), .sel(W_EN), .clk(CLK), .RD1(RD1_17_0[15]), .RD2(RD2_17_0[15]));
  _1bit_RAM _1bit_ram_17 (
    .WD(WD_17_0[16]), .RS1(RS1), .RS2(RS2), .sel(W_EN), .clk(CLK), .RD1(RD1_17_0[16]), .RD2(RD2_17_0[16]));
  _1bit_RAM _1bit_ram_18 (
    .WD(WD_17_0[17]), .RS1(RS1), .RS2(RS2), .sel(W_EN), .clk(CLK), .RD1(RD1_17_0[17]), .RD2(RD2_17_0[17]));

  // Other names for the same wires on the sheet: rd1_0 = RD1_17_0[0]; rd1_1 = RD1_17_0[1]; rd1_2 = RD1_17_0[2];
  //   rd1_3 = RD1_17_0[3]; rd1_4 = RD1_17_0[4]; rd1_5 = RD1_17_0[5]; rd1_6 = RD1_17_0[6]; rd1_7 = RD1_17_0[7];
  //   rd1_8 = RD1_17_0[8]; rd1_9 = RD1_17_0[9]; rd1_10 = RD1_17_0[10]; rd1_11 = RD1_17_0[11]; rd1_12 = RD1_17_0[12];
  //   rd1_13 = RD1_17_0[13]; rd1_14 = RD1_17_0[14]; rd1_15 = RD1_17_0[15]; rd1_16 = RD1_17_0[16];
  //   rd1_17 = RD1_17_0[17]; rd2_0 = RD2_17_0[0]; rd2_1 = RD2_17_0[1]; rd2_2 = RD2_17_0[2]; rd2_3 = RD2_17_0[3];
  //   rd2_4 = RD2_17_0[4]; rd2_5 = RD2_17_0[5]; rd2_6 = RD2_17_0[6]; rd2_7 = RD2_17_0[7]; rd2_8 = RD2_17_0[8];
  //   rd2_9 = RD2_17_0[9]; rd2_10 = RD2_17_0[10]; rd2_11 = RD2_17_0[11]; rd2_12 = RD2_17_0[12]; rd2_13 = RD2_17_0[13];
  //   rd2_14 = RD2_17_0[14]; rd2_15 = RD2_17_0[15]; rd2_16 = RD2_17_0[16]; rd2_17 = RD2_17_0[17]; wd0 = WD_17_0[0];
  //   wd1 = WD_17_0[1]; wd2 = WD_17_0[2]; wd3 = WD_17_0[3]; wd4 = WD_17_0[4]; wd5 = WD_17_0[5]; wd6 = WD_17_0[6];
  //   wd7 = WD_17_0[7]; wd8 = WD_17_0[8]; wd9 = WD_17_0[9]; wd10 = WD_17_0[10]; wd11 = WD_17_0[11];
  //   wd12 = WD_17_0[12]; wd13 = WD_17_0[13]; wd14 = WD_17_0[14]; wd15 = WD_17_0[15]; wd16 = WD_17_0[16];
  //   wd17 = WD_17_0[17]; wEN = W_EN
endmodule
