// Digital circuit 1bit register.dig as structural Verilog
module _1bit_register (
  input  din,
  input  clk,
  input  sel,
  output dout
);

  wire multiplexer_1_out;

  Multiplexer multiplexer_1 (.sel(sel), .in_0(dout), .in_1(din), .out(multiplexer_1_out));
  D_FF d_ff_1 (.D(multiplexer_1_out), .C(clk), .Q(dout));  // open: nQ
endmodule
