// Digital circuit 1bit_FS.dig as structural Verilog
module _1bit_FS (
  input  A,
  input  B,
  input  Bin,
  output S,
  output bout
);

  wire and_1_out, and_2_out, and_3_out, not_1_out, not_2_out, not_3_out;

  not not_1 (not_1_out, A);
  not not_2 (not_2_out, B);
  not not_3 (not_3_out, Bin);
  xor xor_1 (S, A, B, Bin);
  and and_1 (and_1_out, not_1_out, B);
  and and_2 (and_2_out, not_1_out, Bin);
  and and_3 (and_3_out, Bin, B);
  or or_1 (bout, and_1_out, and_2_out, and_3_out);
endmodule
