// Digital circuit 1bit_booth_mul.dig as structural Verilog
module _1bit_booth_mul (
  input  A,
  input  B,
  input  Cin,
  input  H,
  input  D,
  output S,
  output Cout
);

  wire and_1_out, and_2_out, and_3_out, and_4_out, or_1_out, xor_1_out;

  or or_1 (or_1_out, B, Cin);
  xor xor_1 (xor_1_out, D, A);
  and and_1 (and_1_out, H, B);
  and and_2 (and_2_out, H, Cin);
  and and_3 (and_3_out, Cin, B);
  and and_4 (and_4_out, or_1_out, xor_1_out);
  xor xor_2 (S, and_1_out, and_2_out, A);
  or or_2 (Cout, and_3_out, and_4_out);
endmodule
