// Digital circuit 1bit_divier.dig as structural Verilog
module _1bit_divier (
  input  A,
  input  B,
  input  Bin,
  input  sel,
  output Bout,
  output R
);

  wire _1bit_fs_1_s;

  _1bit_FS _1bit_fs_1 (.A(A), .B(B), .Bin(Bin), .S(_1bit_fs_1_s), .bout(Bout));
  Multiplexer multiplexer_1 (.sel(sel), .in_0(_1bit_fs_1_s), .in_1(A), .out(R));
endmodule
