// Digital circuit 1bitreg.dig as structural Verilog
module _1bitreg (
  input  din,
  input  clk,
  input  en,
  output dout
);

  wire multiplexer_1_out;

  Multiplexer multiplexer_1 (.sel(en), .in_0(dout), .in_1(din), .out(multiplexer_1_out));
  D_FF d_ff_1 (.D(multiplexer_1_out), .C(clk), .Q(dout));  // open: nQ
endmodule
