// Digital circuit 1x3 SRAM.dig as structural Verilog
module _1x3_SRAM (
  input  [2:0] WD_2_0,
  input  RS1,
  input  RS2,
  input  W_EN,
  input  CLK,
  output [2:0] RD1_2_0,
  output [2:0] RD2_2_0
);

  _1x1sram _1x1sram_1 (.WD(WD_2_0[0]), .RS1(RS1), .RS2(RS2), .sel(W_EN), .clk(CLK), .RD1(RD1_2_0[0]), .RD2(RD2_2_0[0]));
  _1x1sram _1x1sram_2 (.WD(WD_2_0[1]), .RS1(RS1), .RS2(RS2), .sel(W_EN), .clk(CLK), .RD1(RD1_2_0[1]), .RD2(RD2_2_0[1]));
  _1x1sram _1x1sram_3 (.WD(WD_2_0[2]), .RS1(RS1), .RS2(RS2), .sel(W_EN), .clk(CLK), .RD1(RD1_2_0[2]), .RD2(RD2_2_0[2]));
endmodule
