// Digital circuit 2x2_booth_mul.dig as structural Verilog
module _2x2_booth_mul (
  input  [3:0] A_3_0,
  input  [3:0] B_3_0,
  output [7:0] P_7_0
);

  wire _1bit_booth_mul_1_s, _1bit_booth_mul_2_s, _1bit_booth_mul_3_s, _1bit_booth_mul_5_cout,
       _1bit_booth_mul_5_s, _1bit_booth_mul_6_cout, _1bit_booth_mul_6_s, _1bit_booth_mul_7_cout,
       _1bit_booth_mul_7_s, _1bit_booth_mul_8_cout, _1bit_booth_mul_9_cout, _1bit_booth_mul_9_s,
       _1bit_booth_mul_10_cout, _1bit_booth_mul_10_s, _1bit_booth_mul_11_cout, _1bit_booth_mul_11_s,
       _1bit_booth_mul_12_cout, _1bit_booth_mul_13_cout, _1bit_booth_mul_13_s, _1bit_booth_mul_14_cout,
       _1bit_booth_mul_14_s, _1bit_booth_mul_15_cout, _1bit_booth_mul_15_s, _1bit_booth_mul_16_cout,
       _1bit_booth_mul_17_cout, _1bit_booth_mul_17_s, _1bit_booth_mul_18_cout, _1bit_booth_mul_18_s,
       _1bit_booth_mul_19_cout, _1bit_booth_mul_19_s, _1bit_booth_mul_20_cout, _1bit_booth_mul_21_cout,
       _1bit_booth_mul_21_s, _1bit_booth_mul_22_cout, _1bit_booth_mul_22_s, _1bit_booth_mul_23_cout,
       _1bit_booth_mul_24_cout, _1bit_booth_mul_24_s, _1bit_booth_mul_25_cout, _1bit_booth_mul_26_cout,
       dh_1_d, dh_1_h, dh_2_d, dh_2_h, dh_3_d, dh_3_h, dh_4_d, dh_4_h;

  DH dh_1 (.Xi(B_3_0[0]), .Xi_1(1'b0), .D(dh_1_d), .H(dh_1_h));
  DH dh_2 (.Xi(B_3_0[1]), .Xi_1(B_3_0[0]), .D(dh_2_d), .H(dh_2_h));
  DH dh_3 (.Xi(B_3_0[2]), .Xi_1(B_3_0[1]), .D(dh_3_d), .H(dh_3_h));
  DH dh_4 (.Xi(B_3_0[3]), .Xi_1(B_3_0[2]), .D(dh_4_d), .H(dh_4_h));
  _1bit_booth_mul _1bit_booth_mul_1 (
    .A(1'b0), .B(A_3_0[3]), .Cin(_1bit_booth_mul_5_cout), .H(dh_1_h), .D(dh_1_d), .S(_1bit_booth_mul_1_s));  // open: Cout
  _1bit_booth_mul _1bit_booth_mul_2 (
    .A(_1bit_booth_mul_1_s), .B(A_3_0[3]), .Cin(_1bit_booth_mul_6_cout), .H(dh_2_h), .D(dh_2_d),
    .S(_1bit_booth_mul_2_s));  // open: Cout
  _1bit_booth_mul _1bit_booth_mul_3 (
    .A(_1bit_booth_mul_2_s), .B(A_3_0[3]), .Cin(_1bit_booth_mul_7_cout), .H(dh_3_h), .D(dh_3_d),
    .S(_1bit_booth_mul_3_s));  // open: Cout
  _1bit_booth_mul _1bit_booth_mul_4 (
    .A(_1bit_booth_mul_3_s), .B(A_3_0[3]), .Cin(_1bit_booth_mul_8_cout), .H(dh_4_h), .D(dh_4_d), .S(P_7_0[7]));  // open: Cout
  _1bit_booth_mul _1bit_booth_mul_5 (
    .A(1'b0), .B(A_3_0[3]), .Cin(_1bit_booth_mul_9_cout), .H(dh_1_h), .D(dh_1_d), .S(_1bit_booth_mul_5_s),
    .Cout(_1bit_booth_mul_5_cout));
  _1bit_booth_mul _1bit_booth_mul_6 (
    .A(_1bit_booth_mul_5_s), .B(A_3_0[3]), .Cin(_1bit_booth_mul_10_cout), .H(dh_2_h), .D(dh_2_d),
    .S(_1bit_booth_mul_6_s), .Cout(_1bit_booth_mul_6_cout));
  _1bit_booth_mul _1bit_booth_mul_7 (
    .A(_1bit_booth_mul_6_s), .B(A_3_0[3]), .Cin(_1bit_booth_mul_11_cout), .H(dh_3_h), .D(dh_3_d),
    .S(_1bit_booth_mul_7_s), .Cout(_1bit_booth_mul_7_cout));
  _1bit_booth_mul _1bit_booth_mul_8 (
    .A(_1bit_booth_mul_7_s), .B(A_3_0[3]), .Cin(_1bit_booth_mul_12_cout), .H(dh_4_h), .D(dh_4_d),
    .S(P_7_0[6]), .Cout(_1bit_booth_mul_8_cout));
  _1bit_booth_mul _1bit_booth_mul_9 (
    .A(1'b0), .B(A_3_0[3]), .Cin(_1bit_booth_mul_13_cout), .H(dh_1_h), .D(dh_1_d), .S(_1bit_booth_mul_9_s),
    .Cout(_1bit_booth_mul_9_cout));
  _1bit_booth_mul _1bit_booth_mul_10 (
    .A(_1bit_booth_mul_9_s), .B(A_3_0[3]), .Cin(_1bit_booth_mul_14_cout), .H(dh_2_h), .D(dh_2_d),
    .S(_1bit_booth_mul_10_s), .Cout(_1bit_booth_mul_10_cout));
  _1bit_booth_mul _1bit_booth_mul_11 (
    .A(_1bit_booth_mul_10_s), .B(A_3_0[3]), .Cin(_1bit_booth_mul_15_cout), .H(dh_3_h), .D(dh_3_d),
    .S(_1bit_booth_mul_11_s), .Cout(_1bit_booth_mul_11_cout));
  _1bit_booth_mul _1bit_booth_mul_12 (
    .A(_1bit_booth_mul_11_s), .B(A_3_0[2]), .Cin(_1bit_booth_mul_16_cout), .H(dh_4_h), .D(dh_4_d),
    .S(P_7_0[5]), .Cout(_1bit_booth_mul_12_cout));
  _1bit_booth_mul _1bit_booth_mul_13 (
    .A(1'b0), .B(A_3_0[3]), .Cin(_1bit_booth_mul_17_cout), .H(dh_1_h), .D(dh_1_d), .S(_1bit_booth_mul_13_s),
    .Cout(_1bit_booth_mul_13_cout));
  _1bit_booth_mul _1bit_booth_mul_14 (
    .A(_1bit_booth_mul_13_s), .B(A_3_0[3]), .Cin(_1bit_booth_mul_18_cout), .H(dh_2_h), .D(dh_2_d),
    .S(_1bit_booth_mul_14_s), .Cout(_1bit_booth_mul_14_cout));
  _1bit_booth_mul _1bit_booth_mul_15 (
    .A(_1bit_booth_mul_14_s), .B(A_3_0[2]), .Cin(_1bit_booth_mul_19_cout), .H(dh_3_h), .D(dh_3_d),
    .S(_1bit_booth_mul_15_s), .Cout(_1bit_booth_mul_15_cout));
  _1bit_booth_mul _1bit_booth_mul_16 (
    .A(_1bit_booth_mul_15_s), .B(A_3_0[1]), .Cin(_1bit_booth_mul_20_cout), .H(dh_4_h), .D(dh_4_d),
    .S(P_7_0[4]), .Cout(_1bit_booth_mul_16_cout));
  _1bit_booth_mul _1bit_booth_mul_17 (
    .A(1'b0), .B(A_3_0[3]), .Cin(_1bit_booth_mul_21_cout), .H(dh_1_h), .D(dh_1_d), .S(_1bit_booth_mul_17_s),
    .Cout(_1bit_booth_mul_17_cout));
  _1bit_booth_mul _1bit_booth_mul_18 (
    .A(_1bit_booth_mul_17_s), .B(A_3_0[2]), .Cin(_1bit_booth_mul_22_cout), .H(dh_2_h), .D(dh_2_d),
    .S(_1bit_booth_mul_18_s), .Cout(_1bit_booth_mul_18_cout));
  _1bit_booth_mul _1bit_booth_mul_19 (
    .A(_1bit_booth_mul_18_s), .B(A_3_0[1]), .Cin(_1bit_booth_mul_23_cout), .H(dh_3_h), .D(dh_3_d),
    .S(_1bit_booth_mul_19_s), .Cout(_1bit_booth_mul_19_cout));
  _1bit_booth_mul _1bit_booth_mul_20 (
    .A(_1bit_booth_mul_19_s), .B(A_3_0[0]), .Cin(1'b0), .H(dh_4_h), .D(dh_4_d), .S(P_7_0[3]),
    .Cout(_1bit_booth_mul_20_cout));
  _1bit_booth_mul _1bit_booth_mul_21 (
    .A(1'b0), .B(A_3_0[2]), .Cin(_1bit_booth_mul_24_cout), .H(dh_1_h), .D(dh_1_d), .S(_1bit_booth_mul_21_s),
    .Cout(_1bit_booth_mul_21_cout));
  _1bit_booth_mul _1bit_booth_mul_22 (
    .A(_1bit_booth_mul_21_s), .B(A_3_0[1]), .Cin(_1bit_booth_mul_25_cout), .H(dh_2_h), .D(dh_2_d),
    .S(_1bit_booth_mul_22_s), .Cout(_1bit_booth_mul_22_cout));
  _1bit_booth_mul _1bit_booth_mul_23 (
    .A(_1bit_booth_mul_22_s), .B(A_3_0[0]), .Cin(1'b0), .H(dh_3_h), .D(dh_3_d), .S(P_7_0[2]),
    .Cout(_1bit_booth_mul_23_cout));
  _1bit_booth_mul _1bit_booth_mul_24 (
    .A(1'b0), .B(A_3_0[1]), .Cin(_1bit_booth_mul_26_cout), .H(dh_1_h), .D(dh_1_d), .S(_1bit_booth_mul_24_s),
    .Cout(_1bit_booth_mul_24_cout));
  _1bit_booth_mul _1bit_booth_mul_25 (
    .A(_1bit_booth_mul_24_s), .B(A_3_0[0]), .Cin(1'b0), .H(dh_2_h), .D(dh_2_d), .S(P_7_0[1]),
    .Cout(_1bit_booth_mul_25_cout));
  _1bit_booth_mul _1bit_booth_mul_26 (
    .A(1'b0), .B(A_3_0[0]), .Cin(1'b0), .H(dh_1_h), .D(dh_1_d), .S(P_7_0[0]), .Cout(_1bit_booth_mul_26_cout));
endmodule
