// Digital circuit 3bit register.dig as structural Verilog
module _3bit_register (
  input  clk,
  input  sel,
  input  [2:0] din_2_0,
  output [2:0] dout_2_0
);

  _1bit_register _1bit_register_1 (.din(din_2_0[0]), .clk(clk), .sel(sel), .dout(dout_2_0[0]));
  _1bit_register _1bit_register_2 (.din(din_2_0[1]), .clk(clk), .sel(sel), .dout(dout_2_0[1]));
  _1bit_register _1bit_register_3 (.din(din_2_0[2]), .clk(clk), .sel(sel), .dout(dout_2_0[2]));
endmodule
