// Digital circuit 3bit_adder+sub.dig as structural Verilog
module _3bit_adder_sub (
  input  [2:0] A_2_0,
  input  [2:0] B_2_0,
  input  add_sub,
  output Carry,
  output [2:0] S_2_0
);

  wire C1, C2, xor_1_out, xor_2_out, xor_3_out;

  xor xor_1 (xor_1_out, add_sub, B_2_0[2]);
  Add add_1 (.a(A_2_0[2]), .b(xor_1_out), .c_i(C2), .s(S_2_0[2]), .c_o(Carry));
  xor xor_2 (xor_2_out, add_sub, B_2_0[1]);
  Add add_2 (.a(A_2_0[1]), .b(xor_2_out), .c_i(C1), .s(S_2_0[1]), .c_o(C2));
  xor xor_3 (xor_3_out, add_sub, B_2_0[0]);
  Add add_3 (.a(A_2_0[0]), .b(xor_3_out), .c_i(add_sub), .s(S_2_0[0]), .c_o(C1));

  // Other names for the same wires on the sheet: A0 = A_2_0[0]; A1 = A_2_0[1]; A2 = A_2_0[2]; B0 = B_2_0[0];
  //   B1 = B_2_0[1]; B2 = B_2_0[2]; C0 = add_sub; C3 = Carry; S0 = S_2_0[0]; S1 = S_2_0[1]; S2 = S_2_0[2]
endmodule
