// Digital circuit 3bitalu.dig as structural Verilog
module _3bitalu (
  input  [1:0] op_1_0,
  input  clk,
  input  [2:0] ra_2_0,
  input  [2:0] rb_2_0,
  input  [2:0] wr_2_0,
  input  regEN,
  input  [2:0] wrd_2_0,
  output cf,
  output [2:0] r_2_0
);

  wire [2:0] _8_register_set___3bit_reg_1_a_2_0, _8_register_set___3bit_reg_1_b_2_0;

  _8_register_set___3bit_reg _8_register_set___3bit_reg_1 (
    .clk(clk), .wrd_2_0(wrd_2_0), .ra_2_0(ra_2_0), .rb_2_0(rb_2_0), .wr_2_0(wr_2_0), .regEN(regEN),
    .a_2_0(_8_register_set___3bit_reg_1_a_2_0), .b_2_0(_8_register_set___3bit_reg_1_b_2_0));
  ex1 ex1_1 (
    .A_2_0(_8_register_set___3bit_reg_1_a_2_0), .B_2_0(_8_register_set___3bit_reg_1_b_2_0), .OP_1_0(op_1_0),
    .CF(cf), .R_2_0(r_2_0));
endmodule
