// Digital circuit 3x3 mul.dig as structural Verilog
module _3x3_mul (
  input  [2:0] A_3_0,
  input  [2:0] B_3_0,
  output [2:0] P_2_0,
  output Overflow
);

  wire mul_1_cout, mul_1_s, mul_2_cout, mul_2_s, mul_3_cout, mul_3_s, mul_4_cout, mul_4_s, mul_5_cout,
       mul_5_s, mul_6_cout, mul_7_cout, mul_7_s, mul_8_cout, mul_9_cout;

  mul mul_1 (.Y(B_3_0[2]), .X(A_3_0[2]), .B(mul_2_cout), .Cin(mul_3_cout), .S(mul_1_s), .Cout(mul_1_cout));
  mul mul_2 (.Y(B_3_0[1]), .X(A_3_0[2]), .B(mul_4_cout), .Cin(mul_5_cout), .S(mul_2_s), .Cout(mul_2_cout));
  mul mul_3 (.Y(B_3_0[2]), .X(A_3_0[1]), .B(mul_2_s), .Cin(mul_6_cout), .S(mul_3_s), .Cout(mul_3_cout));
  mul mul_4 (.Y(B_3_0[0]), .X(A_3_0[2]), .B(1'b0), .Cin(mul_7_cout), .S(mul_4_s), .Cout(mul_4_cout));
  mul mul_5 (.Y(B_3_0[1]), .X(A_3_0[1]), .B(mul_4_s), .Cin(mul_8_cout), .S(mul_5_s), .Cout(mul_5_cout));
  mul mul_6 (.Y(B_3_0[2]), .X(A_3_0[0]), .B(mul_5_s), .Cin(1'b0), .S(P_2_0[2]), .Cout(mul_6_cout));
  mul mul_7 (.Y(B_3_0[0]), .X(A_3_0[1]), .B(1'b0), .Cin(mul_9_cout), .S(mul_7_s), .Cout(mul_7_cout));
  mul mul_8 (.Y(B_3_0[1]), .X(A_3_0[0]), .B(mul_7_s), .Cin(1'b0), .S(P_2_0[1]), .Cout(mul_8_cout));
  mul mul_9 (.Y(B_3_0[0]), .X(A_3_0[0]), .B(1'b0), .Cin(1'b0), .S(P_2_0[0]), .Cout(mul_9_cout));
  or or_1 (Overflow, mul_3_s, mul_1_s, mul_1_cout);
endmodule
