// Digital circuit 4 bit CPU.dig as structural Verilog
module _4_bit_CPU (
);

  _9x18bit_RAM _9x18bit_ram_1 ();  // open: WA_3_0, WD_17_0, CLK, RS1_3_0, RS2_3_0, wrEN, RD2_17_0, RD1_17_0
  _6_register_set_of__4bit_reg _6_register_set_of__4bit_reg_1 ();  // open: clk, wrd_3_0, ra_2_0, rb_2_0, wr_2_0, regEN, a_3_0, b_3_0
  _4bit_ALU _4bit_alu_1 ();  // open: A_3_0, B_3_0, OP_1_0, R_3_0, CF, ZF, SF
endmodule
