// Digital circuit +1 [4bit].dig as structural Verilog
module _1__4bit (
  input  [3:0] din_3_0,
  output [3:0] dout_3_0
);

  _4bit_adder _4bit_adder_1 (.A_3_0(din_3_0), .B_3_0(4'b0001), .S_3_0(dout_3_0));  // open: Cout
endmodule
