// Digital circuit 4 bit CPU.dig as structural Verilog
module _4_bit_CPU (
  input  clk,
  input  PC_EN,
  input  [3:0] RAM_WA_3_0,
  input  [17:0] RAM_WD_17_0,
  input  RAM_WR_EN,
  input  [3:0] RAM_RS2_3_0
);

  wire _4bit_alu_1_cf, _4bit_alu_1_sf, _4bit_alu_1_zf, CF, CPU_CLK, IMM_sel, JMP_sel, RD1_7, RD1_8, RD1_9,
       REG_en, SF, ZF;
  wire [1:0] op_1_0;
  wire [3:0] _1__4bit_1_dout_3_0, _4bit_program_counter_1_dout_3_0, _6_register_set_of__4bit_reg_1_a_3_0,
       _6_register_set_of__4bit_reg_1_b_3_0, JMP_address_3_0, multiplexer_1_out, multiplexer_2_out,
       opcode_3_0, R_3_0;
  wire [6:0] _9x18bit_ram_1_rd1_17_0;

  Multiplexer #(.Bits(4)) multiplexer_1 (
    .sel(JMP_sel), .in_0(_1__4bit_1_dout_3_0), .in_1(JMP_address_3_0), .out(multiplexer_1_out));
  _4bit_Program_Counter _4bit_program_counter_1 (
    .clk(CPU_CLK), .din_3_0(multiplexer_1_out), .dout_3_0(_4bit_program_counter_1_dout_3_0));
  _1__4bit _1__4bit_1 (.din_3_0(_4bit_program_counter_1_dout_3_0), .dout_3_0(_1__4bit_1_dout_3_0));
  and and_1 (CPU_CLK, PC_EN, clk);
  _9x18bit_RAM _9x18bit_ram_1 (
    .WA_3_0(RAM_WA_3_0), .WD_17_0(RAM_WD_17_0), .CLK(clk), .RS1_3_0(_4bit_program_counter_1_dout_3_0),
    .RS2_3_0(RAM_RS2_3_0), .wrEN(RAM_WR_EN),
    .RD1_17_0({opcode_3_0, JMP_address_3_0, RD1_9, RD1_8, RD1_7, _9x18bit_ram_1_rd1_17_0}));  // open: RD2_17_0
  Multiplexer #(.Bits(4)) multiplexer_2 (
    .sel(IMM_sel), .in_0(_6_register_set_of__4bit_reg_1_b_3_0),
    .in_1({JMP_address_3_0[0], RD1_9, RD1_8, RD1_7}), .out(multiplexer_2_out));
  _4bit_ALU _4bit_alu_1 (
    .A_3_0(_6_register_set_of__4bit_reg_1_a_3_0), .B_3_0(multiplexer_2_out), .OP_1_0(op_1_0), .R_3_0(R_3_0),
    .CF(_4bit_alu_1_cf), .ZF(_4bit_alu_1_zf), .SF(_4bit_alu_1_sf));
  control_Unit control_unit_1 (
    .opcode_3_0(opcode_3_0), .ZF(ZF), .Imm_sel(IMM_sel), .JMP_sel(JMP_sel), .OP_1_0(op_1_0), .REG_EN(REG_en));
  _6_register_set_of__4bit_reg _6_register_set_of__4bit_reg_1 (
    .clk(CPU_CLK), .WRD_3_0(R_3_0), .ra_2_0(JMP_address_3_0[3:1]),
    .rb_2_0({JMP_address_3_0[0], RD1_9, RD1_8}), .WR_2_0(JMP_address_3_0[3:1]), .REG_EN(REG_en),
    .a_3_0(_6_register_set_of__4bit_reg_1_a_3_0), .b_3_0(_6_register_set_of__4bit_reg_1_b_3_0));
  flag_register flag_register_1 (
    .clk(CPU_CLK), .CF_in(_4bit_alu_1_cf), .ZF_in(_4bit_alu_1_zf), .SF_in(_4bit_alu_1_sf), .CF(CF), .ZF(ZF),
    .SF(SF));

  // Other names for the same wires on the sheet: reg_Bdata_3_0[3:0] = {JMP_address_3_0[0], RD1_9, RD1_8, RD1_7};
  //   reg_BAdrress_2_0[2:0] = {JMP_address_3_0[0], RD1_9, RD1_8}; RD1_10 = JMP_address_3_0[0];
  //   RD1_11 = JMP_address_3_0[1]; reg_AAdrress_2_0[2:0] = JMP_address_3_0[3:1]; RD1_12 = JMP_address_3_0[2];
  //   RD1_13 = JMP_address_3_0[3]
endmodule
