// Digital circuit 4bit ALU.dig as structural Verilog
module _4bit_ALU (
  input  [3:0] A_3_0,
  input  [3:0] B_3_0,
  input  [1:0] OP_1_0,
  output [3:0] R_3_0,
  output CF,
  output ZF,
  output SF
);

  wire [3:0] _4bit_adder_1_s_3_0, _4bit_and_1_r_3_0, _4bit_shr_1_r_3_0;

  _4bit_adder _4bit_adder_1 (.A_3_0(A_3_0), .B_3_0(B_3_0), .S_3_0(_4bit_adder_1_s_3_0), .Cout(CF));
  _4bit_AND _4bit_and_1 (.A_3_0(A_3_0), .B_3_0(B_3_0), .R_3_0(_4bit_and_1_r_3_0));
  _4bit_SHR _4bit_shr_1 (.A_3_0(A_3_0), .B_3_0(B_3_0), .R_3_0(_4bit_shr_1_r_3_0));
  Multiplexer #(.Selector_Bits(2), .Bits(4)) multiplexer_1 (
    .sel(OP_1_0), .in_0(_4bit_adder_1_s_3_0), .in_1(_4bit_and_1_r_3_0), .in_2(_4bit_shr_1_r_3_0),
    .in_3(4'b0000), .out(R_3_0));
  nor nor_1 (ZF, R_3_0[0], R_3_0[1], R_3_0[2], R_3_0[3]);

  assign SF = R_3_0[3];
endmodule
