// Digital circuit 4bit AND.dig as structural Verilog
module _4bit_AND (
  input  [3:0] A_3_0,
  input  [3:0] B_3_0,
  output [3:0] R_3_0
);

  and and_1 (R_3_0[3], A_3_0[3], B_3_0[3]);
  and and_2 (R_3_0[2], A_3_0[2], B_3_0[2]);
  and and_3 (R_3_0[1], A_3_0[1], B_3_0[1]);
  and and_4 (R_3_0[0], A_3_0[0], B_3_0[0]);
endmodule
