// Digital circuit 4bit Program Counter .dig as structural Verilog
module _4bit_Program_Counter (
  input  clk,
  input  [3:0] din_3_0,
  output [3:0] dout_3_0
);

  _4bit_register _4bit_register_1 (.clk(clk), .sel(1'b1), .din_3_0(din_3_0), .dout_3_0(dout_3_0));
endmodule
