// Digital circuit 4bit SHR.dig as structural Verilog
module _4bit_SHR (
  input  [3:0] A_3_0,
  input  [3:0] B_3_0,
  output [3:0] R_3_0
);

  wire nor_1_out, R0, R1, R2, R3;

  Multiplexer #(.Selector_Bits(2)) multiplexer_1 (
    .sel(B_3_0[1:0]), .in_0(A_3_0[3]), .in_1(1'b0), .in_2(1'b0), .in_3(1'b0), .out(R3));
  nor nor_1 (nor_1_out, B_3_0[3], B_3_0[2]);
  Multiplexer #(.Selector_Bits(2)) multiplexer_2 (
    .sel(B_3_0[1:0]), .in_0(A_3_0[2]), .in_1(A_3_0[3]), .in_2(1'b0), .in_3(1'b0), .out(R2));
  Multiplexer #(.Selector_Bits(2)) multiplexer_3 (
    .sel(B_3_0[1:0]), .in_0(A_3_0[1]), .in_1(A_3_0[2]), .in_2(A_3_0[3]), .in_3(1'b0), .out(R1));
  and and_1 (R_3_0[3], nor_1_out, R3);
  and and_2 (R_3_0[2], nor_1_out, R2);
  and and_3 (R_3_0[1], nor_1_out, R1);
  and and_4 (R_3_0[0], nor_1_out, R0);
  Multiplexer #(.Selector_Bits(2)) multiplexer_4 (
    .sel(B_3_0[1:0]), .in_0(A_3_0[0]), .in_1(A_3_0[1]), .in_2(A_3_0[2]), .in_3(A_3_0[3]), .out(R0));

  // Other names for the same wires on the sheet: A0 = A_3_0[0]; A1 = A_3_0[1]; A2 = A_3_0[2]; A3 = A_3_0[3];
  //   Sel[1:0] = B_3_0[1:0]
endmodule
