// Digital circuit 4bit adder.dig as structural Verilog
module _4bit_adder (
  input  [3:0] A_3_0,
  input  [3:0] B_3_0,
  output [3:0] S_3_0,
  output Cout
);

  wire add_1_c_o, add_2_c_o, add_3_c_o;

  Add add_1 (.a(A_3_0[0]), .b(B_3_0[0]), .c_i(1'b0), .s(S_3_0[0]), .c_o(add_1_c_o));
  Add add_2 (.a(A_3_0[1]), .b(B_3_0[1]), .c_i(add_1_c_o), .s(S_3_0[1]), .c_o(add_2_c_o));
  Add add_3 (.a(A_3_0[2]), .b(B_3_0[2]), .c_i(add_2_c_o), .s(S_3_0[2]), .c_o(add_3_c_o));
  Add add_4 (.a(A_3_0[3]), .b(B_3_0[3]), .c_i(add_3_c_o), .s(S_3_0[3]), .c_o(Cout));
endmodule
