// Digital circuit 6 register set of (4bit reg).dig as structural Verilog
module _6_register_set_of__4bit_reg (
  input  clk,
  input  [3:0] WRD_3_0,
  input  [2:0] ra_2_0,
  input  [2:0] rb_2_0,
  input  [2:0] WR_2_0,
  input  REG_EN,
  output [3:0] a_3_0,
  output [3:0] b_3_0
);

  wire and_1_out, and_2_out, and_3_out, and_4_out, and_5_out, and_6_out, decoder_1_out_0, decoder_1_out_1,
       decoder_1_out_2, decoder_1_out_3, decoder_1_out_4, decoder_1_out_5;
  wire [3:0] r0, r1, r2, r3, r4, r5;

  Decoder #(.Selector_Bits(3)) decoder_1 (
    .sel(WR_2_0), .out_0(decoder_1_out_0), .out_1(decoder_1_out_1), .out_2(decoder_1_out_2),
    .out_3(decoder_1_out_3), .out_4(decoder_1_out_4), .out_5(decoder_1_out_5));  // open: out_6, out_7
  and and_1 (and_1_out, REG_EN, decoder_1_out_0);
  and and_2 (and_2_out, REG_EN, decoder_1_out_1);
  and and_3 (and_3_out, REG_EN, decoder_1_out_2);
  and and_4 (and_4_out, REG_EN, decoder_1_out_3);
  and and_5 (and_5_out, REG_EN, decoder_1_out_4);
  and and_6 (and_6_out, REG_EN, decoder_1_out_5);
  _4bit_register _4bit_register_1 (.clk(clk), .sel(and_1_out), .din_3_0(WRD_3_0), .dout_3_0(r0));
  _4bit_register _4bit_register_2 (.clk(clk), .sel(and_2_out), .din_3_0(WRD_3_0), .dout_3_0(r1));
  _4bit_register _4bit_register_3 (.clk(clk), .sel(and_3_out), .din_3_0(WRD_3_0), .dout_3_0(r2));
  _4bit_register _4bit_register_4 (.clk(clk), .sel(and_4_out), .din_3_0(WRD_3_0), .dout_3_0(r3));
  _4bit_register _4bit_register_5 (.clk(clk), .sel(and_5_out), .din_3_0(WRD_3_0), .dout_3_0(r4));
  _4bit_register _4bit_register_6 (.clk(clk), .sel(and_6_out), .din_3_0(WRD_3_0), .dout_3_0(r5));
  Multiplexer #(.Selector_Bits(3), .Bits(4)) multiplexer_1 (
    .sel(ra_2_0), .in_0(r0), .in_1(r1), .in_2(r2), .in_3(r3), .in_4(r4), .in_5(r5), .in_6(4'b0000),
    .in_7(4'b0000), .out(a_3_0));
  Multiplexer #(.Selector_Bits(3), .Bits(4)) multiplexer_2 (
    .sel(rb_2_0), .in_0(r0), .in_1(r1), .in_2(r2), .in_3(r3), .in_4(r4), .in_5(r5), .in_6(4'b0000),
    .in_7(4'b0000), .out(b_3_0));
endmodule
