// Digital circuit control Unit.dig as structural Verilog
module control_Unit (
  input  [3:0] opcode_3_0,
  input  ZF,
  output Imm_sel,
  output JMP_sel,
  output [1:0] OP_1_0,
  output REG_EN
);

  wire and_1_out, and_2_out, and_4_out, and_6_out, JMP_EN, not_1_out, not_2_out, not_3_out, not_4_out,
       not_5_out, not_6_out, not_7_out, or_1_out;

  and and_1 (and_1_out, opcode_3_0[0], not_1_out);
  not not_1 (not_1_out, opcode_3_0[1]);
  and and_2 (and_2_out, not_2_out, not_3_out);
  not not_2 (not_2_out, opcode_3_0[0]);
  not not_3 (not_3_out, opcode_3_0[1]);
  not not_4 (not_4_out, opcode_3_0[3]);
  not not_5 (not_5_out, opcode_3_0[2]);
  not not_6 (not_6_out, opcode_3_0[3]);
  not not_7 (not_7_out, opcode_3_0[2]);
  and and_3 (Imm_sel, opcode_3_0[2], not_4_out);
  and and_4 (and_4_out, not_5_out, not_6_out);
  and and_5 (JMP_EN, not_7_out, opcode_3_0[3]);
  and and_6 (and_6_out, ZF, and_1_out);
  or or_1 (or_1_out, and_6_out, and_2_out);
  or or_2 (REG_EN, and_4_out, Imm_sel);
  and and_7 (JMP_sel, or_1_out, JMP_EN);

  assign OP_1_0 = opcode_3_0[1:0];

  // Other names for the same wires on the sheet: op_0 = opcode_3_0[0]; op_1 = opcode_3_0[1]; type_0 = opcode_3_0[2];
  //   type_1 = opcode_3_0[3]
endmodule
