// Digital circuit flag register.dig as structural Verilog
module flag_register (
  input  clk,
  input  CF_in,
  input  ZF_in,
  input  SF_in,
  output CF,
  output ZF,
  output SF
);

  _1bit_register _1bit_register_1 (.din(CF_in), .clk(clk), .sel(1'b1), .dout(CF));
  _1bit_register _1bit_register_2 (.din(ZF_in), .clk(clk), .sel(1'b1), .dout(ZF));
  _1bit_register _1bit_register_3 (.din(SF_in), .clk(clk), .sel(1'b1), .dout(SF));
endmodule
