// Digital circuit 4bit register.dig as structural Verilog
module _4bit_register (
  input  clk,
  input  sel,
  input  [3:0] din_3_0,
  output [3:0] dout_3_0
);

  _1bit_register _1bit_register_1 (.din(din_3_0[0]), .clk(clk), .sel(sel), .dout(dout_3_0[0]));
  _1bit_register _1bit_register_2 (.din(din_3_0[1]), .clk(clk), .sel(sel), .dout(dout_3_0[1]));
  _1bit_register _1bit_register_3 (.din(din_3_0[2]), .clk(clk), .sel(sel), .dout(dout_3_0[2]));
  _1bit_register _1bit_register_4 (.din(din_3_0[3]), .clk(clk), .sel(sel), .dout(dout_3_0[3]));
endmodule
