// Digital circuit 4bit_FS.dig as structural Verilog
module _4bit_FS (
  input  [3:0] B_3_0,
  input  [3:0] A_3_0,
  output [3:0] S_3_0,
  output bout
);

  wire _1bit_fs_1_bout, _1bit_fs_2_bout, _1bit_fs_3_bout;

  _1bit_FS _1bit_fs_1 (.A(A_3_0[0]), .B(B_3_0[0]), .Bin(1'b0), .S(S_3_0[0]), .bout(_1bit_fs_1_bout));
  _1bit_FS _1bit_fs_2 (.A(A_3_0[1]), .B(B_3_0[1]), .Bin(_1bit_fs_1_bout), .S(S_3_0[1]), .bout(_1bit_fs_2_bout));
  _1bit_FS _1bit_fs_3 (.A(A_3_0[2]), .B(B_3_0[2]), .Bin(_1bit_fs_2_bout), .S(S_3_0[2]), .bout(_1bit_fs_3_bout));
  _1bit_FS _1bit_fs_4 (.A(A_3_0[3]), .B(B_3_0[3]), .Bin(_1bit_fs_3_bout), .S(S_3_0[3]), .bout(bout));
endmodule
