// Digital circuit 4bit_diviver.dig as structural Verilog
module _4bit_diviver (
  input  [3:0] A_3_0,
  input  [3:0] B_3_0,
  output [3:0] Q_3_0,
  output [3:0] R_3_0,
  output exception
);

  wire _1bit_divier_1_bout, _1bit_divier_2_bout, _1bit_divier_2_r, _1bit_divier_3_bout, _1bit_divier_4_bout,
       _1bit_divier_4_r, _1bit_divier_5_bout, _1bit_divier_5_r, _1bit_divier_6_bout, _1bit_divier_7_bout,
       _1bit_divier_8_bout, _1bit_divier_8_r, _1bit_divier_9_bout, _1bit_divier_9_r, _1bit_divier_10_bout,
       _1bit_divier_10_r, _1bit_divier_11_bout, _1bit_divier_12_bout, _1bit_divier_12_r,
       _1bit_divier_13_bout, _1bit_divier_13_r, _1bit_divier_14_bout, _1bit_divier_15_bout,
       _1bit_divier_15_r, _1bit_divier_16_bout;

  nor nor_1 (exception, B_3_0[0], B_3_0[1], B_3_0[2], B_3_0[3]);
  not not_1 (Q_3_0[3], _1bit_divier_1_bout);
  _1bit_divier _1bit_divier_1 (
    .A(1'b0), .B(B_3_0[3]), .Bin(_1bit_divier_2_bout), .sel(_1bit_divier_1_bout), .Bout(_1bit_divier_1_bout));  // open: R
  not not_2 (Q_3_0[2], _1bit_divier_3_bout);
  _1bit_divier _1bit_divier_2 (
    .A(1'b0), .B(B_3_0[2]), .Bin(_1bit_divier_4_bout), .sel(_1bit_divier_1_bout), .Bout(_1bit_divier_2_bout),
    .R(_1bit_divier_2_r));
  _1bit_divier _1bit_divier_3 (
    .A(_1bit_divier_2_r), .B(B_3_0[3]), .Bin(_1bit_divier_5_bout), .sel(_1bit_divier_3_bout),
    .Bout(_1bit_divier_3_bout));  // open: R
  not not_3 (Q_3_0[1], _1bit_divier_6_bout);
  _1bit_divier _1bit_divier_4 (
    .A(1'b0), .B(B_3_0[1]), .Bin(_1bit_divier_8_bout), .sel(_1bit_divier_1_bout), .Bout(_1bit_divier_4_bout),
    .R(_1bit_divier_4_r));
  _1bit_divier _1bit_divier_5 (
    .A(_1bit_divier_4_r), .B(B_3_0[2]), .Bin(_1bit_divier_9_bout), .sel(_1bit_divier_3_bout),
    .Bout(_1bit_divier_5_bout), .R(_1bit_divier_5_r));
  _1bit_divier _1bit_divier_6 (
    .A(_1bit_divier_5_r), .B(B_3_0[3]), .Bin(_1bit_divier_10_bout), .sel(_1bit_divier_6_bout),
    .Bout(_1bit_divier_6_bout));  // open: R
  not not_4 (Q_3_0[0], _1bit_divier_7_bout);
  _1bit_divier _1bit_divier_7 (
    .A(_1bit_divier_10_r), .B(B_3_0[3]), .Bin(_1bit_divier_11_bout), .sel(_1bit_divier_7_bout),
    .Bout(_1bit_divier_7_bout), .R(R_3_0[3]));
  _1bit_divier _1bit_divier_8 (
    .A(A_3_0[3]), .B(B_3_0[0]), .Bin(1'b0), .sel(_1bit_divier_1_bout), .Bout(_1bit_divier_8_bout),
    .R(_1bit_divier_8_r));
  _1bit_divier _1bit_divier_9 (
    .A(_1bit_divier_8_r), .B(B_3_0[1]), .Bin(_1bit_divier_12_bout), .sel(_1bit_divier_3_bout),
    .Bout(_1bit_divier_9_bout), .R(_1bit_divier_9_r));
  _1bit_divier _1bit_divier_10 (
    .A(_1bit_divier_9_r), .B(B_3_0[2]), .Bin(_1bit_divier_13_bout), .sel(_1bit_divier_6_bout),
    .Bout(_1bit_divier_10_bout), .R(_1bit_divier_10_r));
  _1bit_divier _1bit_divier_11 (
    .A(_1bit_divier_13_r), .B(B_3_0[2]), .Bin(_1bit_divier_14_bout), .sel(_1bit_divier_7_bout),
    .Bout(_1bit_divier_11_bout), .R(R_3_0[2]));
  _1bit_divier _1bit_divier_12 (
    .A(A_3_0[2]), .B(B_3_0[0]), .Bin(1'b0), .sel(_1bit_divier_3_bout), .Bout(_1bit_divier_12_bout),
    .R(_1bit_divier_12_r));
  _1bit_divier _1bit_divier_13 (
    .A(_1bit_divier_12_r), .B(B_3_0[1]), .Bin(_1bit_divier_15_bout), .sel(_1bit_divier_6_bout),
    .Bout(_1bit_divier_13_bout), .R(_1bit_divier_13_r));
  _1bit_divier _1bit_divier_14 (
    .A(_1bit_divier_15_r), .B(B_3_0[1]), .Bin(_1bit_divier_16_bout), .sel(_1bit_divier_7_bout),
    .Bout(_1bit_divier_14_bout), .R(R_3_0[1]));
  _1bit_divier _1bit_divier_15 (
    .A(A_3_0[1]), .B(B_3_0[0]), .Bin(1'b0), .sel(_1bit_divier_6_bout), .Bout(_1bit_divier_15_bout),
    .R(_1bit_divier_15_r));
  _1bit_divier _1bit_divier_16 (
    .A(A_3_0[0]), .B(B_3_0[0]), .Bin(1'b0), .sel(_1bit_divier_7_bout), .Bout(_1bit_divier_16_bout),
    .R(R_3_0[0]));

  // Notes on the sheet:
  //   A_3_0: default 6
  //   B_3_0: default 2
endmodule
