// Digital circuit 4bitadd_sub.dig as structural Verilog
module _4bitadd_sub (
  input  [3:0] A_3_0,
  input  [3:0] B_3_0,
  input  selA_S,
  output [3:0] S_3_0,
  output Cout
);

  wire add_1_c_o, add_2_c_o, add_3_c_o, xor_1_out, xor_2_out, xor_3_out, xor_4_out;

  xor xor_1 (xor_1_out, B_3_0[3], selA_S);
  xor xor_2 (xor_2_out, B_3_0[2], selA_S);
  xor xor_3 (xor_3_out, B_3_0[1], selA_S);
  xor xor_4 (xor_4_out, B_3_0[0], selA_S);
  Add add_1 (.a(A_3_0[0]), .b(xor_4_out), .c_i(selA_S), .s(S_3_0[0]), .c_o(add_1_c_o));
  Add add_2 (.a(A_3_0[1]), .b(xor_3_out), .c_i(add_1_c_o), .s(S_3_0[1]), .c_o(add_2_c_o));
  Add add_3 (.a(A_3_0[2]), .b(xor_2_out), .c_i(add_2_c_o), .s(S_3_0[2]), .c_o(add_3_c_o));
  Add add_4 (.a(A_3_0[3]), .b(xor_1_out), .c_i(add_3_c_o), .s(S_3_0[3]), .c_o(Cout));
endmodule
