// Digital circuit 4x3 SRAM.dig as structural Verilog
module _4x3_SRAM (
  input  [2:0] WD_2_0,
  input  [1:0] RA1_1_0,
  input  [1:0] RA2_1_0,
  input  [1:0] WA_1_0,
  input  CLK,
  input  WE,
  output [2:0] RD1_2_0,
  output [2:0] RD2_2_0
);

  wire decoder_1_out_0, decoder_1_out_1, decoder_1_out_2, decoder_1_out_3, rs11, rs12, rs13, rs14, rs21,
       rs22, rs23, rs24, wa1, wa2, wa3, wa4;
  wire [2:0] _1x3_sram_1_rd1_2_0, _1x3_sram_1_rd2_2_0, _1x3_sram_2_rd1_2_0, _1x3_sram_2_rd2_2_0,
       _1x3_sram_3_rd1_2_0, _1x3_sram_3_rd2_2_0, _1x3_sram_4_rd1_2_0, _1x3_sram_4_rd2_2_0;

  Decoder #(.Selector_Bits(2)) decoder_1 (
    .sel(WA_1_0), .out_0(decoder_1_out_0), .out_1(decoder_1_out_1), .out_2(decoder_1_out_2),
    .out_3(decoder_1_out_3));
  Decoder #(.Selector_Bits(2)) decoder_2 (.sel(RA1_1_0), .out_0(rs11), .out_1(rs12), .out_2(rs13), .out_3(rs14));
  Decoder #(.Selector_Bits(2)) decoder_3 (.sel(RA2_1_0), .out_0(rs21), .out_1(rs22), .out_2(rs23), .out_3(rs24));
  and and_1 (wa1, WE, decoder_1_out_0);
  and and_2 (wa2, decoder_1_out_1, WE);
  and and_3 (wa3, decoder_1_out_2, WE);
  and and_4 (wa4, decoder_1_out_3, WE);
  _1x3_SRAM _1x3_sram_1 (
    .WD_2_0(WD_2_0), .RS1(rs11), .RS2(rs21), .W_EN(wa1), .CLK(CLK), .RD1_2_0(_1x3_sram_1_rd1_2_0),
    .RD2_2_0(_1x3_sram_1_rd2_2_0));
  _1x3_SRAM _1x3_sram_2 (
    .WD_2_0(WD_2_0), .RS1(rs12), .RS2(rs22), .W_EN(wa2), .CLK(CLK), .RD1_2_0(_1x3_sram_2_rd1_2_0),
    .RD2_2_0(_1x3_sram_2_rd2_2_0));
  _1x3_SRAM _1x3_sram_3 (
    .WD_2_0(WD_2_0), .RS1(rs13), .RS2(rs23), .W_EN(wa3), .CLK(CLK), .RD1_2_0(_1x3_sram_3_rd1_2_0),
    .RD2_2_0(_1x3_sram_3_rd2_2_0));
  _1x3_SRAM _1x3_sram_4 (
    .WD_2_0(WD_2_0), .RS1(rs14), .RS2(rs24), .W_EN(wa4), .CLK(CLK), .RD1_2_0(_1x3_sram_4_rd1_2_0),
    .RD2_2_0(_1x3_sram_4_rd2_2_0));
  assign RD1_2_0 = _1x3_sram_1_rd1_2_0 | _1x3_sram_2_rd1_2_0 | _1x3_sram_3_rd1_2_0 | _1x3_sram_4_rd1_2_0;  // Or or_1, 3 bits wide
  assign RD2_2_0 = _1x3_sram_1_rd2_2_0 | _1x3_sram_2_rd2_2_0 | _1x3_sram_3_rd2_2_0 | _1x3_sram_4_rd2_2_0;  // Or or_2, 3 bits wide
endmodule
