// Digital circuit 7bitreg.dig as structural Verilog
module _7bitreg (
  input  [6:0] din_6_0,
  input  clk,
  input  en,
  output [6:0] dout_6_0
);

  _1bitreg _1bitreg_1 (.din(din_6_0[0]), .clk(clk), .en(en), .dout(dout_6_0[0]));
  _1bitreg _1bitreg_2 (.din(din_6_0[1]), .clk(clk), .en(en), .dout(dout_6_0[1]));
  _1bitreg _1bitreg_3 (.din(din_6_0[2]), .clk(clk), .en(en), .dout(dout_6_0[2]));
  _1bitreg _1bitreg_4 (.din(din_6_0[3]), .clk(clk), .en(en), .dout(dout_6_0[3]));
  _1bitreg _1bitreg_5 (.din(din_6_0[4]), .clk(clk), .en(en), .dout(dout_6_0[4]));
  _1bitreg _1bitreg_6 (.din(din_6_0[5]), .clk(clk), .en(en), .dout(dout_6_0[5]));
  _1bitreg _1bitreg_7 (.din(din_6_0[6]), .clk(clk), .en(en), .dout(dout_6_0[6]));
endmodule
