// Digital circuit 8 register set ( 3bit reg).dig as structural Verilog
module _8_register_set___3bit_reg (
  input  clk,
  input  [2:0] wrd_2_0,
  input  [2:0] ra_2_0,
  input  [2:0] rb_2_0,
  input  [2:0] wr_2_0,
  input  regEN,
  output [2:0] a_2_0,
  output [2:0] b_2_0
);

  wire and_1_out, and_2_out, and_3_out, and_4_out, and_5_out, and_6_out, and_7_out, and_8_out,
       decoder_1_out_0, decoder_1_out_1, decoder_1_out_2, decoder_1_out_3, decoder_1_out_4, decoder_1_out_5,
       decoder_1_out_6, decoder_1_out_7;
  wire [2:0] r0, r1, r2, r3, r4, r5, r6, r7;

  Decoder #(.Selector_Bits(3)) decoder_1 (
    .sel(wr_2_0), .out_0(decoder_1_out_0), .out_1(decoder_1_out_1), .out_2(decoder_1_out_2),
    .out_3(decoder_1_out_3), .out_4(decoder_1_out_4), .out_5(decoder_1_out_5), .out_6(decoder_1_out_6),
    .out_7(decoder_1_out_7));
  and and_1 (and_1_out, regEN, decoder_1_out_0);
  and and_2 (and_2_out, regEN, decoder_1_out_1);
  and and_3 (and_3_out, regEN, decoder_1_out_2);
  and and_4 (and_4_out, regEN, decoder_1_out_3);
  and and_5 (and_5_out, regEN, decoder_1_out_4);
  and and_6 (and_6_out, regEN, decoder_1_out_5);
  and and_7 (and_7_out, regEN, decoder_1_out_6);
  and and_8 (and_8_out, regEN, decoder_1_out_7);
  _3bit_register _3bit_register_1 (.clk(clk), .sel(and_1_out), .din_2_0(wrd_2_0), .dout_2_0(r0));
  _3bit_register _3bit_register_2 (.clk(clk), .sel(and_2_out), .din_2_0(wrd_2_0), .dout_2_0(r1));
  _3bit_register _3bit_register_3 (.clk(clk), .sel(and_3_out), .din_2_0(wrd_2_0), .dout_2_0(r2));
  _3bit_register _3bit_register_4 (.clk(clk), .sel(and_4_out), .din_2_0(wrd_2_0), .dout_2_0(r3));
  _3bit_register _3bit_register_5 (.clk(clk), .sel(and_5_out), .din_2_0(wrd_2_0), .dout_2_0(r4));
  _3bit_register _3bit_register_6 (.clk(clk), .sel(and_6_out), .din_2_0(wrd_2_0), .dout_2_0(r5));
  _3bit_register _3bit_register_7 (.clk(clk), .sel(and_7_out), .din_2_0(wrd_2_0), .dout_2_0(r6));
  _3bit_register _3bit_register_8 (.clk(clk), .sel(and_8_out), .din_2_0(wrd_2_0), .dout_2_0(r7));
  Multiplexer #(.Bits(3), .Selector_Bits(3)) multiplexer_1 (
    .sel(ra_2_0), .in_0(r0), .in_1(r1), .in_2(r2), .in_3(r3), .in_4(r4), .in_5(r5), .in_6(r6), .in_7(r7),
    .out(a_2_0));
  Multiplexer #(.Selector_Bits(3), .Bits(3)) multiplexer_2 (
    .sel(rb_2_0), .in_0(r0), .in_1(r1), .in_2(r2), .in_3(r3), .in_4(r4), .in_5(r5), .in_6(r6), .in_7(r7),
    .out(b_2_0));
endmodule
