// Digital circuit 9x18bit RAM.dig as structural Verilog
module _9x18bit_RAM (
  input  [3:0] WA_3_0,
  input  [17:0] WD_17_0,
  input  CLK,
  input  [3:0] RS1_3_0,
  input  [3:0] RS2_3_0,
  input  wrEN,
  output [17:0] RD2_17_0,
  output [17:0] RD1_17_0
);

  wire decoder_3_out_0, decoder_3_out_1, decoder_3_out_2, decoder_3_out_3, decoder_3_out_4, decoder_3_out_5,
       decoder_3_out_6, decoder_3_out_7, decoder_3_out_8, en0, en1, en2, en3, en4, en5, en6, en7, en8, RS1_0,
       RS1_1, RS1_2, RS1_3, RS1_4, RS1_5, RS1_6, RS1_7, RS1_8, RS2_0, RS2_1, RS2_2, RS2_3, RS2_4, RS2_5,
       RS2_6, RS2_7, RS2_8;
  wire [17:0] rd1_0, rd1_1, rd1_2, rd1_3, rd1_4, rd1_5, rd1_6, rd1_7, rd1_8, rd2_0, rd2_1, rd2_2, rd2_3,
       rd2_4, rd2_5, rd2_6, rd2_7, rd2_8;

  Decoder #(.Selector_Bits(4)) decoder_1 (
    .sel(RS2_3_0), .out_0(RS2_0), .out_1(RS2_1), .out_2(RS2_2), .out_3(RS2_3), .out_4(RS2_4), .out_5(RS2_5),
    .out_6(RS2_6), .out_7(RS2_7), .out_8(RS2_8));  // open: out_9, out_10, out_11, out_12, out_13, out_14, out_15
  Decoder #(.Selector_Bits(4)) decoder_2 (
    .sel(RS1_3_0), .out_0(RS1_0), .out_1(RS1_1), .out_2(RS1_2), .out_3(RS1_3), .out_4(RS1_4), .out_5(RS1_5),
    .out_6(RS1_6), .out_7(RS1_7), .out_8(RS1_8));  // open: out_9, out_10, out_11, out_12, out_13, out_14, out_15
  Decoder #(.Selector_Bits(4)) decoder_3 (
    .sel(WA_3_0), .out_0(decoder_3_out_0), .out_1(decoder_3_out_1), .out_2(decoder_3_out_2),
    .out_3(decoder_3_out_3), .out_4(decoder_3_out_4), .out_5(decoder_3_out_5), .out_6(decoder_3_out_6),
    .out_7(decoder_3_out_7), .out_8(decoder_3_out_8));  // open: out_9, out_10, out_11, out_12, out_13, out_14, out_15
  and and_1 (en0, wrEN, decoder_3_out_0);
  and and_2 (en1, wrEN, decoder_3_out_1);
  and and_3 (en2, wrEN, decoder_3_out_2);
  and and_4 (en3, wrEN, decoder_3_out_3);
  and and_5 (en4, wrEN, decoder_3_out_4);
  and and_6 (en5, wrEN, decoder_3_out_5);
  and and_7 (en6, wrEN, decoder_3_out_6);
  and and_8 (en7, wrEN, decoder_3_out_7);
  and and_9 (en8, wrEN, decoder_3_out_8);
  _18bit_RAM _18bit_ram_1 (
    .RS1(RS1_0), .RS2(RS2_0), .W_EN(en0), .CLK(CLK), .WD_17_0(WD_17_0), .RD1_17_0(rd1_0), .RD2_17_0(rd2_0));
  _18bit_RAM _18bit_ram_2 (
    .RS1(RS1_1), .RS2(RS2_1), .W_EN(en1), .CLK(CLK), .WD_17_0(WD_17_0), .RD1_17_0(rd1_1), .RD2_17_0(rd2_1));
  _18bit_RAM _18bit_ram_3 (
    .RS1(RS1_2), .RS2(RS2_2), .W_EN(en2), .CLK(CLK), .WD_17_0(WD_17_0), .RD1_17_0(rd1_2), .RD2_17_0(rd2_2));
  _18bit_RAM _18bit_ram_4 (
    .RS1(RS1_3), .RS2(RS2_3), .W_EN(en3), .CLK(CLK), .WD_17_0(WD_17_0), .RD1_17_0(rd1_3), .RD2_17_0(rd2_3));
  _18bit_RAM _18bit_ram_5 (
    .RS1(RS1_4), .RS2(RS2_4), .W_EN(en4), .CLK(CLK), .WD_17_0(WD_17_0), .RD1_17_0(rd1_4), .RD2_17_0(rd2_4));
  _18bit_RAM _18bit_ram_6 (
    .RS1(RS1_5), .RS2(RS2_5), .W_EN(en5), .CLK(CLK), .WD_17_0(WD_17_0), .RD1_17_0(rd1_5), .RD2_17_0(rd2_5));
  _18bit_RAM _18bit_ram_7 (
    .RS1(RS1_6), .RS2(RS2_6), .W_EN(en6), .CLK(CLK), .WD_17_0(WD_17_0), .RD1_17_0(rd1_6), .RD2_17_0(rd2_6));
  _18bit_RAM _18bit_ram_8 (
    .RS1(RS1_7), .RS2(RS2_7), .W_EN(en7), .CLK(CLK), .WD_17_0(WD_17_0), .RD1_17_0(rd1_7), .RD2_17_0(rd2_7));
  _18bit_RAM _18bit_ram_9 (
    .RS1(RS1_8), .RS2(RS2_8), .W_EN(en8), .CLK(CLK), .WD_17_0(WD_17_0), .RD1_17_0(rd1_8), .RD2_17_0(rd2_8));
  assign RD1_17_0 = rd1_0 | rd1_1 | rd1_2 | rd1_3 | rd1_4 | rd1_5 | rd1_6 | rd1_7 | rd1_8;  // Or or_1, 18 bits wide
  assign RD2_17_0 = rd2_0 | rd2_1 | rd2_2 | rd2_3 | rd2_4 | rd2_5 | rd2_6 | rd2_7 | rd2_8;  // Or or_2, 18 bits wide
endmodule
