// Digital circuit DH.dig as structural Verilog
module DH (
  input  Xi,
  input  Xi_1,
  output D,
  output H
);

  wire and_2_out, and_3_out, not_1_out, not_2_out;

  not not_1 (not_1_out, Xi);
  not not_2 (not_2_out, Xi_1);
  and and_1 (D, Xi, not_2_out);
  and and_2 (and_2_out, Xi, not_2_out);
  and and_3 (and_3_out, not_1_out, Xi_1);
  or or_1 (H, and_2_out, and_3_out);
endmodule
