// Digital circuit ex1.dig as structural Verilog
module ex1 (
  input  [2:0] A_2_0,
  input  [2:0] B_2_0,
  input  [1:0] OP_1_0,
  output [2:0] R_2_0,
  output CF
);

  wire [2:0] _3bit_adder_sub_1_s_2_0, not_3bit_1_o_2_0, ror_3bit_1_r_2_0;

  _3bit_register _3bit_register_1 ();  // open: clk, sel, din_2_0, dout_2_0
  _3bit_adder_sub _3bit_adder_sub_1 (
    .A_2_0(A_2_0), .B_2_0(B_2_0), .add_sub(1'b1), .S_2_0(_3bit_adder_sub_1_s_2_0), .Carry(CF));
  ror_3bit ror_3bit_1 (.A_2_0(A_2_0), .B_2_0(B_2_0), .R_2_0(ror_3bit_1_r_2_0));
  not_3bit not_3bit_1 (.A_2_0(A_2_0), .O_2_0(not_3bit_1_o_2_0));
  Multiplexer #(.Selector_Bits(2), .Bits(3)) multiplexer_1 (
    .sel(OP_1_0), .in_0(_3bit_adder_sub_1_s_2_0), .in_1(3'b000), .in_2(ror_3bit_1_r_2_0),
    .in_3(not_3bit_1_o_2_0), .out(R_2_0));

  // Other names for the same wires on the sheet: A[2:0] = A_2_0; B[2:0] = B_2_0
endmodule
