// Digital circuit mul.dig as structural Verilog
module mul (
  input  Y,
  input  X,
  input  B,
  input  Cin,
  output S,
  output Cout
);

  wire and_1_out;

  and and_1 (and_1_out, Y, X);
  Add add_1 (.a(and_1_out), .b(B), .c_i(Cin), .s(S), .c_o(Cout));
endmodule
