// Digital circuit not(3bit).dig as structural Verilog
module not_3bit (
  input  [2:0] A_2_0,
  output [2:0] O_2_0
);

  not not_1 (O_2_0[0], A_2_0[0]);
  not not_2 (O_2_0[1], A_2_0[1]);
  not not_3 (O_2_0[2], A_2_0[2]);
endmodule
