// Digital circuit ror(3bit).dig as structural Verilog
module ror_3bit (
  input  [2:0] A_2_0,
  input  [2:0] B_2_0,
  output [2:0] R_2_0
);

  Multiplexer #(.Selector_Bits(2)) multiplexer_1 (
    .sel(B_2_0[1:0]), .in_0(A_2_0[2]), .in_1(A_2_0[0]), .in_2(A_2_0[1]), .in_3(A_2_0[2]), .out(R_2_0[2]));
  Multiplexer #(.Selector_Bits(2)) multiplexer_2 (
    .sel(B_2_0[1:0]), .in_0(A_2_0[1]), .in_1(A_2_0[2]), .in_2(A_2_0[0]), .in_3(A_2_0[1]), .out(R_2_0[1]));
  Multiplexer #(.Selector_Bits(2)) multiplexer_3 (
    .sel(B_2_0[1:0]), .in_0(A_2_0[0]), .in_1(A_2_0[1]), .in_2(A_2_0[2]), .in_3(A_2_0[0]), .out(R_2_0[0]));

  // Other names for the same wires on the sheet: A0 = A_2_0[0]; A1 = A_2_0[1]; A2 = A_2_0[2]; sh0 = B_2_0[0];
  //   sh1 = B_2_0[1]; B2 = B_2_0[2]
endmodule
